# Fritzing sketch Projeto Alarme - Esquema ESP8266 (saved by Fritzing 0.9.3b)
breadboards: 1

parts:
  Sensore_PIR_HC-SR502 = HC-SR501 Body Sensor Module  # not connected
  Sensore_PIR_HC-SR503 = HC-SR501 Body Sensor Module
  S4 = Magnetic Door Switch [package=reed_switch_plastic]
  U8 = NodeMCU V3.0
  KY-2 = Keyes Relay [package=THT]
  LED1 = RGB LED - (4 legs) [package="5 mm [THT]"]

nets:
  N1: Sensore_PIR_HC-SR503.OUT, U8.D8
  N2: S4.2, U8.D7
  N3: U8.D1, KY-2.power
  N4: U8.D4, LED1.red_cathode
  N5: U8.GND#6, U8.GND#13, U8.GND#16, U8.GND#33
  N6: U8.D5, LED1.green_cathode
  N7: U8.D6, LED1.blue_cathode
  N8: KY-2.GND, LED1.common_anode

notes:
  - GND
  + 5v
  NO -> + buzina
  COM -> + bateria (12v)
  - bateria -> - buzina
  Buzina
  Bateria
  5v

custom parts:
  HC-SR501 Body Sensor Module: Pyroelectric Infrared PIR Motion Sensor Detector Module
  NodeMCU V3.0: ESP8266 based NodeMCU
  Keyes Relay: The Keyes 5V relay module is suitable for SCM development, home appliance control. It uses a 5V~12V TIL control signal which can control DC / AC signal.
