# Fritzing sketch Projeto Alarme - Esquema ESP8266_comming (saved by Fritzing 0.9.3b)
breadboards: 1

parts:
  GSM_SIM_GPSR_SMS_SIM900_SIM1 = SIM800L [package=THT]
  Sensore_PIR_HC-SR502 = HC-SR501 Body Sensor Module  # not connected
  Sensore_PIR_HC-SR503 = HC-SR501 Body Sensor Module
  S4 = Magnetic Door Switch [package=reed_switch_plastic]
  U8 = NodeMCU V3.0
  KY-2 = Keyes Relay [package=THT]
  LED1 = RGB LED - (4 legs) [package="5 mm [THT]"]
  DHT1 = DHT11 Humitidy and Temperature Sensor  # not connected
  Regulador_7805 = Voltage Regulator - 5V [package="TO220 [THT]"]  # not connected

nets:
  N1: GSM_SIM_GPSR_SMS_SIM900_SIM1.VDD, KY-2.signal
  N2: GSM_SIM_GPSR_SMS_SIM900_SIM1.SIM_TXD, U8.D2
  N3: GSM_SIM_GPSR_SMS_SIM900_SIM1.SIM_RXD, U8.D3
  N4: Sensore_PIR_HC-SR503.OUT, U8.D8
  N5: S4.2, U8.D7
  N6: U8.D1, KY-2.power
  N7: U8.D4, LED1.red_cathode
  N8: U8.GND#6, U8.GND#13, U8.GND#16, U8.GND#33
  N9: U8.D5, LED1.green_cathode
  N10: U8.D6, LED1.blue_cathode
  N11: KY-2.GND, LED1.common_anode

notes:
  - GND
  + 5v
  Regulador de tensão 4.1v
  NO -> + buzina
  COM -> + bateria (12v)
  - bateria -> - buzina
  Buzina
  Bateria
  5v

custom parts:
  HC-SR501 Body Sensor Module: Pyroelectric Infrared PIR Motion Sensor Detector Module
  NodeMCU V3.0: ESP8266 based NodeMCU
  Keyes Relay: The Keyes 5V relay module is suitable for SCM development, home appliance control. It uses a 5V~12V TIL control signal which can control DC / AC signal.
  DHT11 Humitidy and Temperature Sensor: DHT11 Humidity and Temperature Sensor
