# Fritzing sketch Projeto Alarme - Esquema (saved by Fritzing 0.9.3b)
breadboards: 1

parts:
  Componente1 = Arduino Uno (Rev3)
  Sensore_PIR_HC-SR502 = HC-SR501 Body Sensor Module
  Sensore_PIR_HC-SR503 = HC-SR501 Body Sensor Module  # not connected
  S4 = Magnetic Door Switch [package=reed_switch_plastic]
  J1 = Piezo Speaker  # not connected
  W5500_Module2 = W5500 Ethernet module [package="DIP (Dual Inline) [THT]"]
  KY-1 = Keyes Relay [package=THT]  # not connected

nets:
  N1: Componente1.D8, Sensore_PIR_HC-SR502.OUT
  N2: Componente1.D10_PWM/SS, W5500_Module2.SCS
  N3: Componente1.D11_PWM/MOSI, W5500_Module2.MOSI
  N4: Componente1.D12/MISO, W5500_Module2.MISO
  N5: Componente1.D13/SCK, W5500_Module2.SCLK
  N6: Componente1.D2, W5500_Module2.INT
  N7: Componente1.D3_PWM, S4.1
  3V3: Componente1.3V3, W5500_Module2.3.3V
  5V: Componente1.5V, Sensore_PIR_HC-SR502.VCC
  GND: Componente1.GND, Sensore_PIR_HC-SR502.GND

notes:
  - GND
  + 5v
  Pendente:
  * ligação SIM800
  NO em buzina +
  COM (+) 12v (bateria)
  - bateria em buzina -
  Buzina
  Bateria
  - GND
  + 3.3V

custom parts:
  HC-SR501 Body Sensor Module: Pyroelectric Infrared PIR Motion Sensor Detector Module
  W5500 Ethernet module: W5500 based SPI Ethernet module for Arduino, etc.
  Keyes Relay: The Keyes 5V relay module is suitable for SCM development, home appliance control. It uses a 5V~12V TIL control signal which can control DC / AC signal.
