# Fritzing sketch Projeto Alarme - Esquemaz Arduino UNO (saved by Fritzing 0.9.3b)
breadboards: 1

parts:
  Componente1 = Arduino Uno (Rev3)
  Sensore_PIR_HC-SR502 = HC-SR501 Body Sensor Module
  Sensore_PIR_HC-SR503 = HC-SR501 Body Sensor Module  # not connected
  S4 = Magnetic Door Switch [package=reed_switch_plastic]
  J1 = Piezo Speaker
  W5500_Module2 = W5500 Ethernet module [package="DIP (Dual Inline) [THT]"]
  KY-1 = Keyes Relay [package=THT]
  GSM_SIM_GPSR_SMS_SIM900_SIM2 = SIM800L [package=THT]  # not connected

nets:
  N1: Componente1.D8, Sensore_PIR_HC-SR502.OUT
  N2: Componente1.D10_PWM/SS, W5500_Module2.SCS
  N3: Componente1.D11_PWM/MOSI, W5500_Module2.MOSI
  N4: Componente1.D12/MISO, W5500_Module2.MISO
  N5: Componente1.D13/SCK, W5500_Module2.SCLK
  N6: Componente1.D2, W5500_Module2.INT
  N7: Componente1.D3_PWM, S4.1
  N8: Componente1.D4, KY-1.power
  N9: Componente1.D7, J1.pin2
  3V3: Componente1.3V3, W5500_Module2.3.3V
  5V: Componente1.5V, Sensore_PIR_HC-SR502.VCC, KY-1.signal
  GND: Componente1.GND, Sensore_PIR_HC-SR502.GND, J1.pin1

notes:
  - GND
  + 5V
  Pendente:
  * ligação GSM SIM800
  NO -> + buzina
  COM -> + bateria (12v)
  - bateria -> - buzina
  Buzina
  Bateria
  - GND
  + 3.3v

custom parts:
  HC-SR501 Body Sensor Module: Pyroelectric Infrared PIR Motion Sensor Detector Module
  W5500 Ethernet module: W5500 based SPI Ethernet module for Arduino, etc.
  Keyes Relay: The Keyes 5V relay module is suitable for SCM development, home appliance control. It uses a 5V~12V TIL control signal which can control DC / AC signal.
