# Fritzing sketch Projeto Alarme - Esquemaz Arduino UNO_coming (saved by Fritzing 0.9.3b)
breadboards: 1

parts:
  Componente1 = Arduino Uno (Rev3)
  Componente2 = RFID-RC522-v2
  GSM_SIM_GPSR_SMS_SIM900_SIM1 = SIM800L [package=THT]
  U5 = RELAY [package=relay-jzc]
  Sensore_PIR_HC-SR502 = HC-SR501 Body Sensor Module
  Sensore_PIR_HC-SR503 = HC-SR501 Body Sensor Module  # not connected
  S4 = Magnetic Door Switch [package=reed_switch_plastic]
  S5 = Momentary Switch [package=ksa_sealed_tac_switch]
  J1 = Piezo Speaker
  W5500_Module1 = W5500 Ethernet module [package="DIP (Dual Inline) [THT]"]  # not connected

nets:
  N1: Componente1.D8, Sensore_PIR_HC-SR502.OUT
  N2: Componente1.D9_PWM, Componente2.RST
  N3: Componente1.D10_PWM/SS, Componente2.SDA
  N4: Componente1.D11_PWM/MOSI, Componente2.MOSI
  N5: Componente1.D12/MISO, Componente2.MISO
  N6: Componente1.D13/SCK, Componente2.SCK
  N7: Componente1.D2, J1.pin2
  N8: Componente1.D3_PWM, GSM_SIM_GPSR_SMS_SIM900_SIM1.SIM_RXD
  N9: Componente1.D4, GSM_SIM_GPSR_SMS_SIM900_SIM1.SIM_TXD
  N10: Componente1.D5_PWM, S4.2
  N11: Componente1.D6_PWM, U5.MAIN
  3V3: Componente1.3V3, Componente2.3.3V
  5V: Componente1.5V, Sensore_PIR_HC-SR502.VCC
  GND: Componente1.GND, Componente2.GND, Sensore_PIR_HC-SR502.GND, S5.1, J1.pin1

notes:
  - GND
  + 5v
  Regulador de tensão
  Buzina
  Relê 12v, NA
  * Pendente coreção ligação SIM800
  * Inclusão do Ethernet
  3.3v GND
  D12
  D11 D2
  D10
  D13

custom parts:
  RFID-RC522-v2: A simple China made RFID-RC522 Reader; do check the pin labels, as this is a MFRC522 based clone.
  HC-SR501 Body Sensor Module: Pyroelectric Infrared PIR Motion Sensor Detector Module
  W5500 Ethernet module: W5500 based SPI Ethernet module for Arduino, etc.
